# Fritzing sketch board (saved by Fritzing 0.7.4b)
breadboards: 1

parts:
  Arduino1 = Arduino
  LED1 = RGB LED - (4 legs) [package="5 mm [THT]"]
  R1 = Resistor [tolerance=±5% resistance=270 package=THT]
  R2 = Resistor [tolerance=±5% resistance=270 package=THT]
  R3 = Resistor [tolerance=±5% resistance=270 package=THT]
  J1 = Piezo Speaker
  R4 = Resistor [tolerance=±5% resistance=10k package=THT]
  R5 = Photocell (LDR) [package=THT]
  T1 = TMP36 Temperature Sensor [package="TO92 [THT]"]
  S1 = Pushbutton [package="[THT]"]
  S2 = Tilt Switch [package=THT]
  R6 = Rotary Potentiometer (Small) [maximum_resistance=100kΩ]
  R7 = Resistor [tolerance=±5% resistance=10k package=THT]
  R8 = Resistor [tolerance=±5% resistance=10k package=THT]
  R9 = Resistor [tolerance=±5% resistance=560 package=THT]
  R10 = Resistor [tolerance=±5% resistance=560 package=THT]
  R11 = Resistor [tolerance=±5% resistance=560 package=THT]
  LED4 = LED - 5mm [color="Red (660nm)" package="5 mm [THT]"]
  LED5 = LED - 5mm [color="Green (555nm)" package="5 mm [THT]"]
  LED6 = LED - 5mm [color="Red (660nm)" package="5 mm [THT]"]

nets:
  GND: Arduino1.GND, J1.pin1, R4.Pin_0, T1.+Vs, T1.GND, S2.Pin_1, R6.leg1, R8.Pin_1, LED4.cathode, LED5.cathode, LED6.cathode
  N1: Arduino1.D11, R1.Pin_0
  N2: Arduino1.D10, R2.Pin_0
  N3: Arduino1.D9, R3.Pin_0
  N4: Arduino1.D8, S2.Pin_2, R7.Pin_0
  N5: Arduino1.D7, R9.Pin_0
  N6: Arduino1.D6, R10.Pin_0
  N7: Arduino1.D5, R11.Pin_0
  N8: Arduino1.D3, J1.pin2
  N9: Arduino1.D2, S1.Pin_3, S1.Pin_4, R8.Pin_0
  N10: Arduino1.+5V, LED1.common_anode, R5.pin_1, S1.Pin_1, S1.Pin_2, R6.leg2, R7.Pin_1
  N11: Arduino1.A0, R4.Pin_1, R5.pin_0
  N12: Arduino1.A1, T1.Vout
  N13: Arduino1.A2, R6.wiper
  N14: LED1.red_cathode, R1.Pin_1
  N15: LED1.green_cathode, R2.Pin_1
  N16: LED1.blue_cathode, R3.Pin_1
  N17: R9.Pin_1, LED4.anode
  N18: R10.Pin_1, LED6.anode
  N19: R11.Pin_1, LED5.anode

notes:
  10kΩ
